// Logisim project Wv1.circ as structural Verilog: 6 circuits, main circuit main
module main (
  input  in_1,
  input  in_2,
  input  in_3,
  input  in_4,
  output out_5
);

  Circ_Aula28_02 circ_aula28_02_1 (.out_5(out_5), .A(in_3), .B(in_1), .C(in_2), .D(in_4));
endmodule

module Add_1 (
  input  A,
  input  B,
  input  Vem_1,
  output S,
  output Vai_1
);

  wire and_1_out, and_2_out, or_1_out, xor_1_out;

  xor xor_1 (xor_1_out, B, A);
  or or_1 (or_1_out, Vem_1, B);
  and and_1 (and_1_out, B, Vem_1);
  xor xor_2 (S, Vem_1, xor_1_out);
  and and_2 (and_2_out, or_1_out, A);
  or or_2 (Vai_1, and_2_out, and_1_out);
endmodule

module Add_4 (
  input  [3:0] B,
  input  [3:0] A,
  output Overflow,
  output [3:0] SOMA
);

  wire add_1_2_vai_1, add_1_3_vai_1, add_1_4_vai_1;

  Add_1 add_1_1 (.S(SOMA[3]), .Vai_1(Overflow), .A(A[3]), .B(B[3]), .Vem_1(add_1_2_vai_1));
  Add_1 add_1_2 (.S(SOMA[2]), .Vai_1(add_1_2_vai_1), .A(A[2]), .B(B[2]), .Vem_1(add_1_3_vai_1));
  Add_1 add_1_3 (.S(SOMA[1]), .Vai_1(add_1_3_vai_1), .A(A[1]), .B(B[1]), .Vem_1(add_1_4_vai_1));
  Add_1 add_1_4 (.S(SOMA[0]), .Vai_1(add_1_4_vai_1), .A(A[0]), .B(B[0]), .Vem_1(1'b0));
endmodule

module _2_S (
  input  [3:0] in_1,
  output [3:0] out_2
);

  wire [3:0] not_2_out;

  not not_1 (not_2_out[1], in_1[1]);
  not not_2 (not_2_out[0], in_1[0]);
  not not_3 (not_2_out[3], in_1[3]);
  not not_4 (not_2_out[2], in_1[2]);
  Add_4 add_4_1 (.B(4'b0001), .A(not_2_out), .SOMA(out_2));  // open: Overflow
endmodule

module Subtrator (
  input  [3:0] B,
  input  [3:0] A,
  output [3:0] out_3
);

  wire [3:0] n2_s_1_out_2;

  _2_S u_2_s_1 (.in_1(B), .out_2(n2_s_1_out_2));
  Add_4 add_4_1 (.B(n2_s_1_out_2), .A(A), .SOMA(out_3));  // open: Overflow
endmodule

module Circ_Aula28_02 (
  input  A,
  input  B,
  input  C,
  input  D,
  output out_5
);

  wire and_1_out, nand_1_out, nor_1_out, nor_2_out, or_1_out, xnor_1_out;

  xnor xnor_1 (xnor_1_out, ~A, B);  // XNOR_Gate
  and and_1 (and_1_out, ~C, ~D);  // AND_Gate
  or or_1 (or_1_out, A, ~D);  // OR_Gate
  nor nor_1 (nor_1_out, B, C);
  nor nor_2 (nor_2_out, xnor_1_out, and_1_out);
  nand nand_1 (nand_1_out, or_1_out, nor_1_out);
  xnor xnor_2 (out_5, nor_2_out, nand_1_out);
endmodule
